# Fritzing sketch Untitled Sketch (saved by Fritzing 0.9.3b)
breadboards: 1

parts:
  A1 = Arduino UNO R4 WiFi
  C1 = Ceramic Capacitor [capacitance=100nF package="100 mil [THT, multilayer]"]
  S1 = Pushbutton [package="[THT]"]
  パーツ1 = Thumb Joystick
  Grove1 = Grove OLED 128x96
  R1 = Resistor [tolerance=±1% resistance=10k package=THT]

nets (from the schematic view):
  VCC: A1.Pin_8, A1.Pin_27, S1.Pin_1, S1.Pin_2, パーツ1.VCC, Grove1.VCC
  N1: A1.Pin_9, A1.Pin_25, A1.Pin_30, パーツ1.GND
  N2: A1.Pin_12, パーツ1.HORZ
  N3: A1.Pin_13, パーツ1.VERT
  N4: A1.Pin_42, C1.0, S1.Pin_3, S1.Pin_4, R1.Pin_0
  N5: A1.Pin_50, Grove1.SDA
  N6: A1.Pin_51, Grove1.SCL
  N7: C1.1, Grove1.GND, R1.Pin_1

custom parts:
  Arduino UNO R4 WiFi: The Arduino UNO R4 WiFi merges the RA4M1 microprocessor from Renesas with the ESP32-S3 from Espressif, creating an all-in-one tool for makers with enhanced processing power and a diverse array of new peripherals.
